# Fritzing sketch LCD RGBLED and Buttons (saved by Fritzing 0.9.3b)
breadboards: 1

parts:
  S1 = Pushbutton [package="[THT]"]
  S2 = Pushbutton [package="[THT]"]
  S3 = Pushbutton [package="[THT]"]
  R1 = Resistor [tolerance=±5% resistance=10k package=THT]
  R2 = Resistor [tolerance=±5% resistance=10k package=THT]
  R3 = Resistor [tolerance=±5% resistance=10k package=THT]
  LED1 = RGB LED (com. cathode, rgb) [package="5 mm [THT]"]
  R4 = Resistor [tolerance=±5% resistance=220 package=THT]
  R5 = Resistor [tolerance=±5% resistance=220 package=THT]
  R6 = Resistor [tolerance=±5% resistance=220 package=THT]
  LCD1 = LCD screen
  R7 = Trimmer Potentiometer [maximum_resistance=10kΩ package=THT]
  Part1 = Arduino Uno (Rev3) - ICSP
  R8 = Resistor [tolerance=±5% resistance=220 package=THT]
  Q1 = Basic FET P-Channel [package="TO220 [THT]"]
  D1 = Rectifier Diode [part_number=1N4001 package="300 mil [THT]"]
  BAT1 = Battery Holders [package=battery_20mm_pth_compact]
  M1 = DC Motor

nets:
  N1: S1.Pin_1, S1.Pin_2
  N2: S1.Pin_3, S1.Pin_4, R3.Pin_0, Part1.A1
  N3: S2.Pin_1, S2.Pin_2
  N4: S2.Pin_3, S2.Pin_4, R2.Pin_0, Part1.A0
  VSS: S3.Pin_1, S3.Pin_2, LED1.green_anode, LCD1.VSS, LCD1.R/W, LCD1.LED-, R7.leg1, Part1.GND, Q1.source, BAT1.-
  N5: S3.Pin_3, S3.Pin_4, R1.Pin_0, Part1.D2
  VDD: R1.Pin_1, R2.Pin_1, R3.Pin_1, LCD1.VDD, R7.leg2, Part1.5V, R8.Pin_0
  N6: LED1.red_anode, R5.Pin_1
  N7: LED1.common_cathode, R6.Pin_1
  N8: LED1.blue_anode, R4.Pin_1
  N9: R4.Pin_0, Part1.D11_PWM/MOSI
  N10: R5.Pin_0, Part1.D9_PWM
  N11: R6.Pin_0, Part1.D10_PWM/SS
  N12: LCD1.V0, R7.wiper
  N13: LCD1.RS, Part1.D12/MISO
  N14: LCD1.E, Part1.D8
  N15: LCD1.DB4, Part1.D7
  N16: LCD1.DB5, Part1.D6_PWM
  N17: LCD1.DB6, Part1.D5_PWM
  N18: LCD1.DB7, Part1.D4
  N19: LCD1.LED+, R8.Pin_1
  N20: Part1.D13/SCK, Q1.gate
  N21: Q1.drain, D1.anode, M1.pin_1
  N22: D1.cathode, BAT1.+, M1.pin_2

notes:
  Battery
  Green min, Yellow plus
